# Fritzing sketch Signage (saved by Fritzing 0.9.3b)

parts:
  Raspberry_Pi_1 = Raspberry Pi 3 [part_number=RPI-3-V1.2]
  CAMERA1 = TTL Serial JPEG Camera  # not connected
  KY-1 = Keyes Relay [package=THT]
  R1 = Resistor [tolerance=±5% resistance=220 package=THT]
  U1 = DIODE-ZENER [package=diode-zener]  # not connected
  LED1 = smd LED [color="Red (633nm)" package="1206 [SMD]"]
  F1 = Fan - Ventilador [package=THT]
  S1 = SWITCH-MOMENTARY-2 [package=tactile_switch_tall]  # not connected
  S2 = SWITCH-MOMENTARY-2 [package=tactile_switch_tall]
  hc-sr1 = hc-sr04
  Power_plug2 = Power plug

nets:
  N1: Raspberry_Pi_1.GPIO3, KY-1.signal
  GND: Raspberry_Pi_1.GND, F1.GND, S2.2, hc-sr1.GND
  N2: Raspberry_Pi_1.GIPO22, hc-sr1.Trig
  3V3: Raspberry_Pi_1.3V3, F1.5V
  N3: Raspberry_Pi_1.GIPO21, S2.1
  N4: Raspberry_Pi_1.GIPO23, hc-sr1.Echo
  5V: Raspberry_Pi_1.5V, KY-1.power, hc-sr1.VCC
  N5: KY-1.C, Power_plug2.VCC
  N6: KY-1.NO, R1.Pin_0
  N7: LED1.cathode, Power_plug2.GND

notes:
  Main Power In
  To Digital Screen
  Ultrasonic Sensor
  Cooling Fan
  Relay Module
  Indicator Setup
  Reset
  Power
  Camera Module
  RPI

custom parts:
  TTL Serial JPEG Camera: TTL Serial JPEG Camera with NTSC Out
  Keyes Relay: The Keyes 5V relay module is suitable for SCM development, home appliance control. It uses a 5V~12V TIL control signal which can control DC / AC signal.
  Fan - Ventilador: Ventilador de 2 pines, se encuentra comunmente en computadoras de escritorio
